// Logisim project 2 Bit ALU.circ as structural Verilog: 2 circuits, main circuit main
module main (
  input  [1:0] Operand_B,
  input  [1:0] Operand_A,
  input  Carry_In,
  input  BiInvert,
  input  [1:0] Comparator_Op,
  input  [2:0] ALU_Op,
  output [1:0] Result,
  output Carry_Borrow,
  output [1:0] MUL_RES,
  output Carry
);

  wire ALU0_carry_borrow;

  _1_Bit_ALU ALU0 (
    .Carry_In(Carry_In), .BiInvert(BiInvert), .Operand_B(Operand_B[0]), .Operand_A(Operand_A[0]),
    .Carry_Borrow(ALU0_carry_borrow), .Comparator_Op(Comparator_Op), .ALU_Op(ALU_Op), .Result(Result[0]));
  _1_Bit_ALU ALU1 (
    .Carry_In(ALU0_carry_borrow), .BiInvert(BiInvert), .Operand_B(Operand_B[1]), .Operand_A(Operand_A[1]),
    .Carry_Borrow(Carry_Borrow), .Comparator_Op(Comparator_Op), .ALU_Op(ALU_Op), .Result(Result[1]));
  Multiplier #(.width(1)) multiplier_1 (
    .a(Operand_A[1]), .b(Operand_B[1]), .out(MUL_RES[1]), .cin(Carry_In), .cout(Carry));

  assign MUL_RES[0] = MUL_RES[1];

  // Notes on the sheet:
  //   2 Bit ALU
endmodule

module _1_Bit_ALU (
  input  Operand_B,
  input  Operand_A,
  input  Carry_In,
  input  BiInvert,
  input  [1:0] Comparator_Op,
  input  [2:0] ALU_Op,
  output Result,
  output Carry_Borrow
);

  wire adder_1_out, and_1_out, comparator_1_eq, comparator_1_gt, comparator_1_lt, multiplexer_1_out,
       multiplexer_2_out, not_1_out, not_2_out, or_1_out, xor_1_out;

  not not_1 (not_1_out, Operand_B);
  Multiplexer multiplexer_1 (.in0(Operand_B), .in1(not_1_out), .out(multiplexer_1_out), .sel(BiInvert));  // open: en
  not not_2 (not_2_out, Operand_A);
  and and_1 (and_1_out, Operand_A, Operand_B);
  or or_1 (or_1_out, Operand_A, Operand_B);
  xor xor_1 (xor_1_out, Operand_A, Operand_B);
  Adder #(.width(1)) adder_1 (
    .a(Operand_A), .b(multiplexer_1_out), .out(adder_1_out), .cin(Carry_In), .cout(Carry_Borrow));
  Comparator #(.width(1)) comparator_1 (
    .a(Operand_A), .b(Operand_B), .gt(comparator_1_gt), .eq(comparator_1_eq), .lt(comparator_1_lt));
  Multiplexer #(.select(2)) multiplexer_2 (
    .in1(comparator_1_gt), .in2(comparator_1_eq), .in3(comparator_1_lt), .out(multiplexer_2_out),
    .sel(Comparator_Op));  // open: in0, en
  Multiplexer #(.select(3)) multiplexer_3 (
    .in0(not_2_out), .in1(and_1_out), .in2(or_1_out), .in3(xor_1_out), .in4(adder_1_out),
    .in5(multiplexer_2_out), .out(Result), .sel(ALU_Op));  // open: in6, in7, en

  // Notes on the sheet:
  //   1 Bit ALU
endmodule
